# Fritzing sketch TerzoAssignemnt-Giardino (saved by Fritzing 0.9.5d)
breadboards: 1

parts:
  Componente1 = Arduino Uno (Rev3) - ICSP
  Componente2 = Bluetooth HC-05 Macho
  U1 = ESP32S-HiLetgo [part_number=ESP32S-HiLetgo]
  D1 = LTE-302 [package=lte-302]
  D2 = LTE-302 [package=lte-302]
  D3 = LTE-302 [package=lte-302]
  D4 = LTE-302 [package=lte-302]
  D5 = LTE-302 [package=lte-302]
  R1 = PHOTOCELL [package=photocell]
  T1 = TMP36 Temperature Sensor [package="TO92 [THT]"]
  R2 = Resistor [tolerance=±5% resistance=220 package="0402 [SMD]"]  # not connected
  R3 = Resistor [tolerance=±5% resistance=220 package="0402 [SMD]"]
  R4 = Resistor [tolerance=±5% resistance=220 package="0402 [SMD]"]
  R5 = Resistor [tolerance=±5% resistance=220 package="0402 [SMD]"]
  R6 = Resistor [tolerance=±5% resistance=220 package="0402 [SMD]"]
  R7 = Resistor [tolerance=±5% resistance=220 package="0402 [SMD]"]
  R8 = Resistor [tolerance=±5% resistance=220 package="0402 [SMD]"]
  D6 = LTE-302 [package=lte-302]  # not connected
  J1 = Basic Servo
  R9 = Resistor [tolerance=±5% resistance=220 package="0402 [SMD]"]  # not connected
  R10 = Resistor [tolerance=±5% resistance=220 package="0402 [SMD]"]  # not connected

nets:
  N1: Componente1.D9_PWM, J1.pulse
  N2: Componente1.D2, Componente2.RXD
  N3: Componente1.D3_PWM, Componente2.TXD
  N4: Componente1.D4, R3.Pin_0
  N5: Componente1.D5_PWM, R5.Pin_0
  N6: Componente1.D6_PWM, R4.Pin_0
  N7: Componente1.D7, R6.Pin_0
  VCC: Componente1.5V, Componente2.VCC, J1.vcc
  GND: Componente1.GND, Componente2.GND, D2.C, D3.C, D4.C, D5.C, J1.gnd
  N8: U1.GPIO39, R1.P$1, R8.Pin_0
  N9: U1.GPIO34, T1.Vout
  N10: U1.GPIO6, T1.GND, R8.Pin_1
  N11: U1.GPIO7, D1.C, R1.P$2, T1.+Vs
  N12: U1.GPIO1, R7.Pin_1
  N13: D1.A, R7.Pin_0
  N14: D2.A, R3.Pin_1
  N15: D3.A, R5.Pin_1
  N16: D4.A, R4.Pin_1
  N17: D5.A, R6.Pin_1

custom parts:
  ESP32S-HiLetgo: HiLetgo ESP-WROOM-32 ESP32 ESP-32S Development Board 2.4GHz Dual-Mode WiFi + Bluetooth Dual Cores Microcontroller The ESP32 integrated with Antenna switches, RF Balun, power amplifiers, low-noise amplifiers, filters, and management modules, and the entire solution occupies the least area of PCB. 2.4 GHz Wi-Fi plus Bluetooth dual-mode chip, with TSMC Ultra-low power consumption 40nm technology,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
